# Fritzing sketch arduinosan (saved by Fritzing 0.9.4)
breadboards: 1

parts:
  Part1 = Adafruit Metro with Headers [part_number="Adafruit #2488"]
  Part2 = Adafruit MAX31865 RTD Sensor Breakout [part_number="Adafruit #3328"]
  DHT1 = DHT11 Humitidy and Temperature Sensor
  R1 = Resistor [tolerance=±5% resistance=4.7 package=THT]

nets:
  N1: Part1.SCK, Part2.SCLK
  N2: Part1.MISO, Part2.SDO
  N3: Part1.MOSI, Part2.SDI
  N4: Part1.SS, Part2.CS
  N5: Part1.IO2, DHT1.DATA, R1.Pin_1
  +5V: Part1.+5V, Part2.VIN, DHT1.VDD, R1.Pin_0
  GND: Part1.GND, Part2.GND, DHT1.GND

custom parts:
  Adafruit Metro with Headers: We sure love the ATmega328 here at Adafruit, and we use them a lot for our own projects. The processor has plenty of GPIO, Analog inputs, hardware UART SPI and I2C, timers and PWM galore - just enough for most simple projects. When we need to go small, we use a Pro Trinket 3V or 5V, but when size isn't as much of a concern, and an USB-serial converter is required, we reach for an Adafruit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
  Adafruit MAX31865 RTD Sensor Breakout: For precision temperature sensing, nothing beats a Platinum RTD. Resistance temperature detectors (RTDs) are temperature sensors that contain a resistor that changes resistance value as its temperature changes, basically a kind of thermistor. In this sensor, the resistor is actually a small strip of Platinum with a resistance of 100 ohms at 0°C, thus the name PT100. Compared to most NTC/PTC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
  DHT11 Humitidy and Temperature Sensor: DHT11 Humidity and Temperature Sensor
